# Fritzing sketch montagem_fritz (saved by Fritzing 0.9.3b)
breadboards: 1

parts:
  R1 = Photocell (LDR) [package=THT]
  DHT1 = DHT11 Humitidy and Temperature Sensor
  U1 = NodeMCU V1.0
  Componente1 = FC-28 Soil Hygrometer Module - Probe
  Componente2 = FC-28 Soil Hygrometer Module
  D1 = Diode [package=diode-1n4148]
  D2 = Diode [package=diode-1n4148]
  R2 = Resistor [tolerance=±20% resistance=10k package="2010 [SMD]"]

nets:
  N1: R1.pin_0, D2.A, R2.Pin_0
  N2: R1.pin_1, U1.D8
  VDD: DHT1.VDD, U1.3V3, R2.Pin_1
  N3: DHT1.DATA, U1.D5
  GND: DHT1.GND, U1.GND, Componente2.GND
  N4: U1.D7, Componente2.VCC
  N5: U1.A0, D1.C, D2.C
  N6: Componente1.POS, Componente2.POS
  N7: Componente1.NEG, Componente2.NEG
  N8: Componente2.AO, D1.A

custom parts:
  DHT11 Humitidy and Temperature Sensor: DHT11 Humidity and Temperature Sensor
  NodeMCU V1.0: ESP8266 based NodeMCU
  FC-28 Soil Hygrometer Module - Probe: The FC-28 is a soil hygrometer module that uses the Texas Instruments LM393 comparator chip to provide an analog measurement of soil humidity.
  FC-28 Soil Hygrometer Module: The FC-28 is a soil hygrometer module that uses the Texas Instruments LM393 comparator chip to provide an analog measurement of soil humidity. The digital output is high when soil moisture is over a certain threshold, as determined by adjusting the potentiometer.
